# Fritzing sketch fritzing buggy layout (saved by Fritzing 1.0.2b)
breadboards: 1

parts:
  BAT1 = 6xAA battery  # not connected
  A1 = Arduino UNO R4 WiFi
  M1 = MH Sensor Series 4-pin IR Sensor/Line follower [package=THT]
  M2 = MH Sensor Series 4-pin IR Sensor/Line follower [package=THT]
  A2 = HuskyLens-Vision-Sensor_1  # not connected
  S2 = SPST Slide Switch [package="SIP THT"]
  HC-SR04_Sensor_1 = HC-SR04 Ultrasonic Distance Sensor
  IC2 = L293D [package=THT]  # not connected
  M4 = gear-motor-encoder-magnet  # not connected
  M5 = gear-motor-encoder-magnet  # not connected

nets:
  N1: A1.Pin_7, A1.Pin_19, HC-SR04_Sensor_1.VCC
  N2: A1.Pin_8, A1.Pin_27, M1.pin4, M2.pin3, S2.COM
  N3: A1.Pin_9, A1.Pin_10, A1.Pin_30, M1.pin3, M2.pin2, HC-SR04_Sensor_1.GND
  N4: A1.Pin_37, M2.pin1
  N5: A1.Pin_38, M1.pin2
  N6: A1.Pin_42, HC-SR04_Sensor_1.ECHO
  N7: A1.Pin_43, HC-SR04_Sensor_1.TRIG

custom parts:
  Arduino UNO R4 WiFi: The Arduino UNO R4 WiFi merges the RA4M1 microprocessor from Renesas with the ESP32-S3 from Espressif, creating an all-in-one tool for makers with enhanced processing power and a diverse array of new peripherals.
  MH Sensor Series 4-pin IR Sensor/Line follower: modified version of FC-51 from Peter Van Epp (vanepp in forums) This is the 4-pin version of IR line follower module, using the TCRT5000 sensor and LM393 comparator This one has the analogue output pin, in addition to the Digital pin which is set by the trimmer. The Analog pin can feed an Arduino ADC input, for much better level sensing options and less drift than the crappy potentiometer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
  HuskyLens-Vision-Sensor_1: Huskylens is an easy-to-use AI Camera | Vision Sensor. DFrobot Huskylens is equipped with multiple functions, such as face recognition, object tracking, object recognition, line tracking, color recognition, and tag(QR code) recognition.
  SPST Slide Switch: SPST slide switch with inline 100mil spacing through hole connection terminals
  gear-motor-encoder-magnet: Generic gear motor, 3V to 6V, dual output shafts, 1:48 gear ratio with magnet for wheel encoder
